# Fritzing sketch toilite (saved by Fritzing 0.9.3b)
breadboards: 1

parts:
  U1 = attiny85 [package=dip]
  LED1 = RGB LED (com. cathode, rbg) [package="5 mm [THT]"]
  R1 = Photocell (LDR) [package=THT]
  S1 = Pushbutton [package="[THT]"]
  R2 = Resistor [tolerance=±5% resistance=150 package="0603 [SMD]"]
  R3 = Resistor [tolerance=±5% resistance=100 package="0603 [SMD]"]
  R4 = Resistor [tolerance=±5% resistance=100 package="0603 [SMD]"]
  R5 = TRIMPOT [package=3386u]
  Q1 = NPN-Transistor [package="TO92 [THT]"]
  R6 = Resistor [tolerance=±5% resistance=100 package=THT]
  Q2 = NPN-Transistor [package="TO92 [THT]"]
  PIR1 = PIR sensor
  U2 = Voltage Regulator - 3.3V [package="TO220 [THT]"]
  C1 = Electrolytic Capacitor [capacitance=1μF package="0405 [SMD, electrolytic]"]
  C2 = Electrolytic Capacitor [capacitance=1μF package="0405 [SMD, electrolytic]"]
  VCC1 = Battery block 9V

nets:
  N1: U1.Pin_3, R2.Pin_1
  GND: U1.Pin_4, R1.pin_0, R5.CW, R6.Pin_0, Q2.E, PIR1.GND, U2.GND, C1.-, C2.+, VCC1.-
  N2: U1.Pin_5, R4.Pin_1
  N3: U1.Pin_6, R3.Pin_1
  N4: U1.Pin_7, S1.Pin_1, S1.Pin_2, R6.Pin_1
  N5: U1.Pin_8, S1.Pin_3, S1.Pin_4, R5.CCW, PIR1.VDD, U2.input_voltage, C2.-
  N6: LED1.red_anode, R2.Pin_0
  N7: LED1.common_cathode, Q1.C
  N8: LED1.blue_anode, R4.Pin_0
  N9: LED1.green_anode, R3.Pin_0
  N10: R1.pin_1, R5.WIPER, Q1.B
  N11: Q1.E, Q2.C
  N12: Q2.B, PIR1.SIG
  N13: U2.output_voltage, C1.+, VCC1.+
